# Fritzing sketch fanboy (saved by Fritzing 0.9.4)
circuit board: 8.00448cm x 4.8cm
breadboards: 1

parts:
  FAN1 = Header 4 [package=molex-1x4_lock]
  TEMP1 = Header 2 [package=molex-1x2_lock]
  R_RPM1 = Resistor [tolerance=±5% resistance=4.7k package=THT]
  FAN2 = Header 4 [package=molex-1x4_lock]
  R_RPM2 = Resistor [tolerance=±5% resistance=4.7k package=THT]
  FAN3 = Header 4 [package=molex-1x4_lock]
  R_RPM3 = Resistor [tolerance=±5% resistance=4.7k package=THT]
  FAN4 = Header 4 [package=molex-1x4_lock]
  R_RPM4 = Resistor [tolerance=±5% resistance=4.7k package=THT]
  TEMP2 = Header 2 [package=molex-1x2_lock]
  12V = Screw terminal - 2 pins [package=THT]
  Pro_Micro = SparkFun Pro Micro
  R_TEMP1 = Resistor [tolerance=±5% resistance=10k package=THT]
  R_TEMP2 = Resistor [tolerance=±5% resistance=10k package=THT]
  PWR = male pin header, 2 pins [form="♂ (male)"]

nets:
  N1: FAN1.1, FAN2.1, FAN3.1, FAN4.1, 12V.pin1, Pro_Micro.GND, R_TEMP1.Pin_0, R_TEMP2.Pin_0
  N2: FAN1.2, FAN2.2, FAN3.2, FAN4.2, 12V.pin2, PWR.pin2
  N3: FAN1.3, R_RPM1.Pin_1, Pro_Micro.8
  N4: FAN1.4, Pro_Micro.9
  N5: TEMP1.1, R_RPM1.Pin_0, R_RPM2.Pin_0, R_RPM3.Pin_0, R_RPM4.Pin_0, TEMP2.1, Pro_Micro.VCC
  N6: TEMP1.2, Pro_Micro.A1, R_TEMP1.Pin_1
  N7: FAN2.3, R_RPM2.Pin_1, Pro_Micro.7
  N8: FAN2.4, Pro_Micro.6
  N9: FAN3.3, R_RPM3.Pin_1, Pro_Micro.4
  N10: FAN3.4, Pro_Micro.5
  N11: FAN4.3, R_RPM4.Pin_1, Pro_Micro.2
  N12: FAN4.4, Pro_Micro.10
  N13: TEMP2.2, Pro_Micro.A0, R_TEMP2.Pin_1
  N14: Pro_Micro.RAW, PWR.pin1

notes:
  FanBoy v1.0
  lynix.github.io/fanboy

custom parts:
  SparkFun Pro Micro: The Pro Micro is similar to the Pro Mini except with an ATmega32U4 on board. The USB transceiver inside the 32U4 allows us to add USB connectivity on-board and do away with bulky external USB interface. Based on: https://github.com/unorthodox-engineers/unorthodox-arduino/blob/master/Unorthodox/fritzing/parts/Pro%20Micro.fzpz
